# Fritzing sketch Blink_2LEDs (saved by Fritzing 0.9.3b)
circuit board: 8.46667cm x 5.64444cm
breadboards: 1

parts:
  R1 = Resistor [tolerance=±5% resistance=330 power=0.25 package=THT]
  LED = LED - 5mm [color="Red (633nm)" current=0.030 package="5 mm [THT]"]
  Part1 = Arduino Uno (Rev3)
  LED1 = LED - 5mm [color="Blue (470nm)" current=0.030 package="5 mm [THT]"]
  R2 = Resistor [tolerance=±5% resistance=330 power=0.25 package=THT]

nets:
  N1: R1.Pin_0, Part1.GND, R2.Pin_0
  N2: R1.Pin_1, LED.cathode
  N3: LED.anode, Part1.D13/SCK
  N4: Part1.D12/MISO, LED1.anode
  N5: LED1.cathode, R2.Pin_1
