# Fritzing sketch RGB_LED (saved by Fritzing 0.9.3b)
breadboards: 1

parts:
  Part1 = Arduino Uno (Rev3)
  LED1 = RGB LED (com. cathode, rgb) [package="5 mm [THT]"]
  R1 = Resistor [tolerance=±5% resistance=470 package=THT]
  R2 = Resistor [tolerance=±5% resistance=430 package=THT]
  R3 = Resistor [tolerance=±5% resistance=430 package=THT]

nets:
  N1: Part1.D9_PWM, R1.Pin_0
  N2: Part1.D10_PWM/SS, R2.Pin_0
  N3: Part1.D11_PWM/MOSI, R3.Pin_0
  N4: Part1.GND, LED1.common_cathode
  N5: LED1.red_anode, R1.Pin_1
  N6: LED1.green_anode, R2.Pin_1
  N7: LED1.blue_anode, R3.Pin_1
