# Fritzing sketch SolenoidMosModule_PowerSupply (saved by Fritzing 0.9.3b)

parts:
  M1 = hcmmodu0083 [package=THT]
  L1 = Solenoid
  JACK2 = 2.1mm Barrel Jack with Terminal Block
  Part1 = Arduino Uno (Rev3)

nets:
  N1: M1.pin1, Part1.D9_PWM
  N2: M1.pin2, Part1.5V
  N3: M1.pin3, Part1.GND
  N4: M1.pin4, JACK2.NEG
  N5: M1.pin5, JACK2.POS
  N6: M1.pin6, L1.pin2
  N7: M1.pin7, L1.pin1

custom parts:
  hcmmodu0083: hcmmodu0083 IRF540 Mosfet driver module
